# Fritzing sketch meteo (saved by Fritzing 0.9.3b)
circuit board: 8.46667cm x 5.64444cm
breadboards: 1

parts:
  Q1 = NPN-Transistor [package="TO92 [THT]"]
  Attiny85 = attiny85 [package=dip]
  R1 = Resistor [tolerance=±5% resistance=220 package=THT]
  ESP-01 = ESP8266-01 WiFi Module [part_number=ESP8266]
  24LC32 = 24LC32 [package=THT]
  DHT22 = DHT22 Humidity and Temperature Sensor
  BMP180 = Barometric Pressure Sensor - BMP180 Breakout (GY-68)

nets:
  VDD: Q1.E, ESP-01.connector1, ESP-01.connector5, 24LC32.WP_-_Write_Protect, 24LC32.+V, DHT22.VDD, BMP180.VCC
  N1: Q1.B, R1.Pin_0
  N2: Q1.C, Attiny85.Pin_8
  GND: Attiny85.Pin_4, ESP-01.connector6, 24LC32.A0, 24LC32.A1, 24LC32.A2, 24LC32.0V, DHT22.GND, BMP180.GND
  N3: Attiny85.Pin_5, ESP-01.connector2, 24LC32.SDA_-_I2C_Data, BMP180.SDA
  N4: Attiny85.Pin_6, R1.Pin_1
  N5: Attiny85.Pin_7, ESP-01.connector4, 24LC32.SCL_-_I2C_Clock, BMP180.SCL
  N6: ESP-01.connector0, DHT22.DATA

notes:
  scl
  sda
  debug
